# Fritzing sketch schematic (saved by Fritzing 0.9.3b)

parts:
  Composant3 = Arduino Uno (Rev3)
  Composant4 = Arduino Uno (Rev3)
  M3 = Niren can bus module [package=THT]
  M4 = Niren can bus module [package=THT]
  R2 = Rotary Potentiometer (Small) [maximum_resistance=100kΩ package=THT]

nets:
  N1: Composant3.D10_PWM/SS, M3.pin3
  N2: Composant3.D11_PWM/MOSI, M3.pin5
  N3: Composant3.D12/MISO, M3.pin4
  N4: Composant3.D13/SCK, M3.pin6
  N5: Composant3.D2, M3.pin7
  N6: Composant3.5V, M3.pin1
  N7: Composant3.GND, M3.pin2
  N8: Composant4.A0, R2.wiper
  N9: Composant4.D10_PWM/SS, M4.pin3
  N10: Composant4.D11_PWM/MOSI, M4.pin5
  N11: Composant4.D12/MISO, M4.pin4
  N12: Composant4.D13/SCK, M4.pin6
  N13: Composant4.D2, M4.pin7
  N14: Composant4.5V, M4.pin1
  N15: Composant4.GND, M4.pin2, R2.leg1
  N16: M3.pin8, M3.pin9
  N17: M3.pin10, M4.pin10
  N18: M3.pin11, M4.pin11
  N19: M4.pin8, M4.pin9

custom parts:
  Niren can bus module: Niren can bus module availabe on ebay and others. Pcb view assumes that you unsolder the 7 pin header and resolder it on the bottom of the module to connect to the pcb. The two jumpers and the can bus connector remain on the top of the board and don't appear in pcb view.
